# Fritzing sketch iChan (saved by Fritzing 0.9.1b)
breadboards: 1

parts:
  パーツ1 = Arduino Leonardo (Rev3b)
  R1 = Resistor [tolerance=±5% resistance=220 package=THT]
  R2 = Resistor [tolerance=±5% resistance=220 package=THT]
  R3 = Resistor [tolerance=±5% resistance=220 package=THT]
  R4 = Resistor [tolerance=±5% resistance=220 package=THT]
  J1 = Basic Force Sensing Resistor (FSR) [package=THT]
  J2 = Basic Force Sensing Resistor (FSR) [package=THT]
  J3 = Basic Force Sensing Resistor (FSR) [package=THT]
  J4 = Basic Force Sensing Resistor (FSR) [package=THT]

nets:
  N1: パーツ1.5V, J1.pin_0, J2.pin_0, J3.pin_0, J4.pin_0
  N2: パーツ1.GND, R1.Pin_1, R2.Pin_1, R3.Pin_1, R4.Pin_1
  N3: パーツ1.A0, R1.Pin_0, J1.pin_1
  N4: パーツ1.A1, R2.Pin_0, J2.pin_1
  N5: パーツ1.A2, R3.Pin_0, J3.pin_1
  N6: パーツ1.A3, R4.Pin_0, J4.pin_1
